# Fritzing sketch Esquema (saved by Fritzing 0.9.3b)
breadboards: 2

parts:
  LCD1 = TFT 1.8 inch 160x128 w SD  # not connected
  J1 = Piezo Speaker
  J6 = Screw terminal - 2 pins [package=THT]
  J7 = Screw terminal - 2 pins [package=THT]
  J8 = Screw terminal - 2 pins [package=THT]
  J9 = Screw terminal - 2 pins [package=THT]
  J10 = Screw terminal - 2 pins [package=THT]
  Componente6 = Arduino Nano (Rev3.0)
  S3 = Pushbutton [package="[THT]"]
  S4 = Pushbutton [package="[THT]"]
  CD2 = CD4051
  J12 = Screw terminal - 2 pins [package=THT]
  T2 = LM35 Temperature Sensor [package="TO92 [THT]"]
  Q2 = Basic FET N-Channel [package="TO220 [THT]"]
  Q3 = Basic FET N-Channel [package="TO220 [THT]"]
  Componente7 = ACS712 Current Sensor Module
  Componente8 = ACS712 Current Sensor Module
  Componente9 = ACS712 Current Sensor Module
  Componente10 = ACS712 Current Sensor Module
  R14 = Resistor [tolerance=±5% resistance=4.7k package=THT]
  R15 = Resistor [tolerance=±5% resistance=10k package=THT]
  R16 = Resistor [tolerance=±5% resistance=680 package=THT]
  R17 = Resistor [tolerance=±5% resistance=1k package=THT]
  R18 = Resistor [tolerance=±5% resistance=1k package=THT]
  R19 = Resistor [tolerance=±5% resistance=10k package=THT]
  M1 = DC Motor
  R20 = Resistor [tolerance=±5% resistance=1k package=THT]
  R21 = Resistor [tolerance=±5% resistance=1M package=THT]
  R22 = Resistor [tolerance=±5% resistance=1k package=THT]
  R23 = Resistor [tolerance=±5% resistance=1M package=THT]

nets:
  GND: J1.pin1, J7.pin2, Componente6.GND, S3.Pin_1, S3.Pin_2, S4.Pin_1, S4.Pin_2, CD2.Inhibit, CD2.VSS, Componente7.GND, Componente8.GND, Componente9.GND, Componente10.GND
  N1: J1.pin2, Componente6.D4
  N2: J6.pin1, Componente6.A1
  N3: J7.pin1, Componente6.VIN
  N4: J8.pin2, R15.Pin_1, M1.pin_1
  N5: J9.pin1, Q3.source, R23.Pin_1
  N6: J10.pin1, Q3.drain, R19.Pin_1
  N7: Componente6.D1/TX, S4.Pin_3, S4.Pin_4
  N8: Componente6.D0/RX, R20.Pin_0
  N9: Componente6.D2, S3.Pin_3, S3.Pin_4
  N10: Componente6.D3, R22.Pin_0
  N11: Componente6.D5, CD2.Input_A
  N12: Componente6.D6, CD2.Input_B
  N13: Componente6.D7, CD2.Input_C
  VCC: Componente6.5V, CD2.VDD, T2.+Vs, Componente7.VCC, Componente8.VCC, Componente9.VCC, Componente10.VCC
  N14: Componente6.A5, T2.Vout
  N15: Componente6.A4, R18.Pin_1, R19.Pin_0
  N16: Componente6.A3, R14.Pin_1, R15.Pin_0
  N17: Componente6.A2, R16.Pin_1, R17.Pin_0
  N18: Componente6.A0, CD2.In/Out
  N19: CD2.Chan_3, Componente10.OUT
  N20: CD2.Chan_0, Componente9.OUT
  N21: CD2.Chan_1, Componente8.OUT
  N22: CD2.Chan_2, Componente7.OUT
  N23: J12.pin2, R17.Pin_1
  N24: T2.GND, Q2.source, R14.Pin_0, R16.Pin_0, R18.Pin_0, R21.Pin_1
  N25: Q2.gate, R20.Pin_1, R21.Pin_0
  N26: Q2.drain, M1.pin_2
  N27: Q3.gate, R22.Pin_1, R23.Pin_0

custom parts:
  TFT 1.8 inch 160x128 w SD: This is a generic 1.8 tft spi lcd display available on ebay and others. The 1.8" display has 128x160 color pixels.

// code stored in the sketch: Untitled.ino

