# Fritzing sketch esquemafuenteatx (saved by Fritzing 0.9.3b)
circuit board: 16.2003cm x 9.95554cm
breadboards: 2

parts:
  CD1 = CD4051
  Componente1 = ACS712 Current Sensor Module
  Componente2 = ACS712 Current Sensor Module
  Componente3 = ACS712 Current Sensor Module
  Componente4 = ACS712 Current Sensor Module
  Componente5 = Arduino Nano (Rev3.0)
  Q1 = Basic FET N-Channel [package="TO220 [THT]"]
  LCD1 = TFT 1.8 inch 160x128 w SD
  S1 = Pushbutton [package="[THT]"]
  S2 = Pushbutton [package="[THT]"]
  J1 = Piezo Speaker
  Reg1 = DC-DC CONVERTER [part_number=80633 package=dc-dc_converter]
  J2 = Screw terminal - 2 pins [package=THT]
  J3 = Screw terminal - 2 pins [package=THT]
  J4 = Screw terminal - 2 pins [package=THT]
  J5 = Screw terminal - 2 pins [package=THT]
  R3 = Resistor [tolerance=±5% resistance=220 package=THT]
  R4 = Resistor [tolerance=±5% resistance=220 package=THT]
  R5 = Resistor [tolerance=±5% resistance=220 package=THT]
  R6 = Resistor [tolerance=±5% resistance=220 package=THT]
  R7 = Resistor [tolerance=±5% resistance=220 package=THT]
  R8 = Resistor [tolerance=±5% resistance=220 package=THT]
  J6 = Screw terminal - 2 pins [package=THT]
  J7 = Screw terminal - 2 pins [package=THT]
  J8 = Screw terminal - 2 pins [package=THT]
  J9 = Screw terminal - 2 pins [package=THT]
  LED1 = LED - 5mm [color="Red (633nm)" package="5 mm [THT]"]
  R9 = Resistor [tolerance=±5% resistance=220 package=THT]
  R11 = Resistor [tolerance=±5% resistance=220 package=THT]
  R12 = Resistor [tolerance=±5% resistance=220 package=THT]
  LED2 = LED - 5mm [color="Red (633nm)" package="5 mm [THT]"]
  LED3 = LED - 5mm [color="Red (633nm)" package="5 mm [THT]"]
  J10 = Screw terminal - 2 pins [package=THT]
  LED4 = LED - 5mm [color="Red (633nm)" package="5 mm [THT]"]
  R13 = Resistor [tolerance=±5% resistance=220 package=THT]
  T1 = LM35 Temperature Sensor [package="TO92 [THT]"]
  J11 = Screw terminal - 2 pins [package=THT]

nets:
  N1: CD1.In/Out, Componente5.A0
  GND: CD1.Inhibit, CD1.VSS, Componente1.GND, Componente2.GND, Componente3.GND, Componente4.GND, Componente5.GND, Q1.source, LCD1.pin2, S1.Pin_1, S1.Pin_2, S2.Pin_1, S2.Pin_2, J1.pin1, J5.pin1, J6.pin2, J7.pin2, J8.pin2, LED1.anode, LED3.anode, J10.pin1, LED4.anode, T1.GND
  N2: CD1.Input_C, Componente5.D7
  N3: CD1.Input_B, Componente5.D6
  N4: CD1.Input_A, Componente5.D5
  N5: CD1.Chan_3, Componente4.OUT
  N6: CD1.Chan_0, Componente3.OUT
  N7: CD1.Chan_1, Componente2.OUT
  N8: CD1.Chan_2, Componente1.OUT
  VCC: CD1.VDD, Componente1.VCC, Componente2.VCC, Componente3.VCC, Componente4.VCC, Componente5.5V, LCD1.pin_1, T1.+Vs
  N9: Componente1.INPUT+, R9.Pin_0
  N10: Componente1.INPUT-, J3.pin2, R3.Pin_0, J11.pin1
  N11: Componente2.INPUT+, R12.Pin_0
  N12: Componente2.INPUT-, J4.pin2, R5.Pin_0
  N13: Componente3.INPUT+, R11.Pin_0
  N14: Componente3.INPUT-, Componente5.A1, J5.pin2
  N15: Componente4.INPUT+, J6.pin1
  N16: Componente4.INPUT-, Reg1.OUT+, R7.Pin_0
  N17: Componente5.D2, S1.Pin_3, S1.Pin_4
  N18: Componente5.D3, S2.Pin_3, S2.Pin_4
  N19: Componente5.D4, J1.pin2
  N20: Componente5.D8, LCD1.pin4
  N21: Componente5.D9, LCD1.pin_5
  N22: Componente5.D10, LCD1.pin3
  N23: Componente5.D11/MOSI, LCD1.pin_6
  N24: Componente5.D12/MISO, Q1.gate
  N25: Componente5.A5, T1.Vout
  N26: Componente5.A4, R7.Pin_1, R8.Pin_0
  N27: Componente5.A3, R3.Pin_1, R4.Pin_0
  N28: Componente5.A2, R5.Pin_1, R6.Pin_0
  N29: Componente5.3V3, LCD1.pin_8
  N30: Componente5.D13/SCK, LCD1.pin_7
  N31: Q1.drain, J11.pin2
  N32: Reg1.OUT-, R8.Pin_1
  N33: Reg1.IN-, J2.pin1
  N34: Reg1.IN+, J2.pin2
  N35: J3.pin1, R4.Pin_1
  N36: J4.pin1, R6.Pin_1
  N37: J7.pin1, R11.Pin_1, LED3.cathode
  N38: J8.pin1, LED1.cathode, R9.Pin_1
  N39: J9.pin1, R12.Pin_1, LED2.cathode
  N40: J9.pin2, LED2.anode
  N41: J10.pin2, R13.Pin_1
  N42: LED4.cathode, R13.Pin_0

custom parts:
  TFT 1.8 inch 160x128 w SD: This is a generic 1.8 tft spi lcd display available on ebay and others. The 1.8" display has 128x160 color pixels.
  DC-DC CONVERTER: WYHP 5A constant current/voltage manufactured by Shenzhen Weiyapuhua Technology Co., Ltd

// code stored in the sketch: Untitled.ino

